# Fritzing sketch Analysis-Sketch (saved by Fritzing 0.9.3b)
breadboards: 1

parts:
  Composant1 = Arduino Uno (Rev3)
  S1 = Momentary Switch [package=tactile-pth]
  IR1 = TSOP312.., 314.. [package=THT]

nets:
  N1: Composant1.D12/MISO, S1.2
  N2: Composant1.D13/SCK, IR1.GND
  N3: Composant1.3V3, IR1.Data
  N4: Composant1.GND, S1.4, IR1.Vs
